# Fritzing sketch obniz-00 (saved by Fritzing 0.9.3b)
breadboards: 1

parts:
  obniz1 = obniz
  R1 = Resistor [tolerance=±1% resistance=1k package=THT]
  LED1 = LED - 5mm [color="Red (633nm)" package="5 mm [THT]"]

nets:
  N1: obniz1.io0, LED1.anode
  N2: obniz1.io1, R1.Pin_1
  N3: R1.Pin_0, LED1.cathode

custom parts:
  obniz: obniz is a microcontroller board based
