# Fritzing sketch obniz-02 (saved by Fritzing 0.9.3b)
breadboards: 1

parts:
  obniz1 = obniz
  Buzzer = Piezo Speaker
  R1 = Resistor [tolerance=±1% resistance=1k package=THT]

nets:
  N1: obniz1.io2, R1.Pin_0
  N2: obniz1.io3, Buzzer.pin1
  N3: Buzzer.pin2, R1.Pin_1

notes:
  +

custom parts:
  obniz: obniz is a microcontroller board based
